// Logisim project gr8.circ as structural Verilog: 6 circuits, main circuit main
module main (
  input  [7:0] PC_in,
  input  in_2,
  output [7:0] PC
);

  wire Clock_out, multiplexer_1_out, not_1_out, PC_Shift_out, R_W_Shift_out, RB_SHIFTER_out, REG_SHIFTER_out,
       REG_SHIFTER_q4, RX_SHIFTER_out;
  wire [3:0] ALU_o_p, ALU_o_p_2, ALU_o_p_3, IR_q_2, multiplexer_2_out;
  wire [7:0] MAR_q, multiplexer_3_out, multiplexer_4_out, RA_q, ram_1_data, RB_q, register_bank_1_data_out,
       RX_q;
  wire [15:0] RZ_q;
  wire [15:12] ALU_o_p_4;
  wire [19:0] IR_q, MBR_q, rom_1_data;

  Clock Clock (.out(Clock_out));
  PC u_PC (.PC_In(PC_in), .Clock(Clock_out), .PC_Enable(PC_Shift_out), .Reset(in_2), .PC_Out(PC));
  Shift_Register #(.length(6)) REG_SHIFTER (
    .in(REG_SHIFTER_out), .clk(Clock_out), .out(REG_SHIFTER_out), .q4(REG_SHIFTER_q4));  // open: shift, load, clr, d0, q0, d1, q1, d2, q2, d3, q3, d4, d5, q5
  Shift_Register #(.length(5)) PC_Shift (
    .in(PC_Shift_out), .clk(Clock_out), .out(PC_Shift_out));  // open: shift, load, clr, d0, q0, d1, q1, d2, q2, d3, q3, d4, q4
  Register MAR (.D(PC), .en(PC_Shift_out), .Q(MAR_q), .clk(Clock_out), .clr(in_2));
  ROM #(.dataWidth(20)) rom_1 (.addr(MAR_q), .data(rom_1_data));  // open: sel
  Multiplexer #(.disabled(0), .enable("false")) multiplexer_1 (
    .in0(R_W_Shift_out), .in1(REG_SHIFTER_out), .out(multiplexer_1_out), .sel(REG_SHIFTER_q4));
  Shift_Register #(.length(6)) R_W_Shift (
    .in(R_W_Shift_out), .clk(Clock_out), .out(R_W_Shift_out));  // open: shift, load, clr, d0, q0, d1, q1, d2, q2, d3, q3, d4, q4, d5, q5
  Register #(.width(20)) MBR (.D(rom_1_data), .Q(MBR_q), .clk(Clock_out), .clr(in_2));  // open: en
  Register #(.width(20)) IR (
    .D(MBR_q), .Q({IR_q[19:16], IR_q_2, IR_q[11:0]}), .clk(Clock_out), .clr(in_2));  // open: en
  Multiplexer #(.width(4), .disabled(0), .enable("false")) multiplexer_2 (
    .in0(IR_q[11:8]), .in1(IR_q_2), .out(multiplexer_2_out), .sel(REG_SHIFTER_q4));
  Multiplexer #(.width(8), .disabled(0), .enable("false")) multiplexer_3 (
    .in0(IR_q[7:0]), .in1(RX_q), .out(multiplexer_3_out), .sel(RX_SHIFTER_out));
  Shift_Register #(.length(6)) RX_SHIFTER (
    .in(RX_SHIFTER_out), .clk(Clock_out), .out(RX_SHIFTER_out));  // open: shift, load, clr, d0, q0, d1, q1, d2, q2, d3, q3, d4, q4, d5, q5
  not not_1 (not_1_out, R_W_Shift_out);
  Register_Bank register_bank_1 (
    .Data_in(RZ_q[7:0]), .Rx__4bit(multiplexer_2_out), .Clock(PC_Shift_out),
    .Data_Out(register_bank_1_data_out), .R_W(multiplexer_1_out));
  Register RA (.D(register_bank_1_data_out), .Q(RA_q), .clk(Clock_out), .clr(in_2));  // open: en
  RAM #(.bus("separate")) ram_1 (
    .addr(multiplexer_3_out), .din(RB_q), .data(ram_1_data), .str(not_1_out), .clk(Clock_out),
    .ld(R_W_Shift_out));  // open: sel, clr
  Register RB (.D(multiplexer_4_out), .Q(RB_q), .clk(Clock_out), .clr(in_2));  // open: en
  Multiplexer #(.width(8), .enable("false")) multiplexer_4 (
    .in0(ram_1_data), .out(multiplexer_4_out), .sel(RB_SHIFTER_out));  // open: in1
  ALU__8_bit ALU (.A(RA_q), .B(RB_q), .Opcode(IR_q[19:16]), .O_p({ALU_o_p_4, ALU_o_p_3, ALU_o_p_2, ALU_o_p}));
  Shift_Register #(.length(6)) RB_SHIFTER (
    .in(RB_SHIFTER_out), .clk(Clock_out), .out(RB_SHIFTER_out));  // open: shift, load, clr, d0, q0, d1, q1, d2, q2, d3, q3, d4, q4, d5, q5
  Register RX (.D(ram_1_data), .Q(RX_q), .clk(Clock_out), .clr(in_2));  // open: en
  Hex_Digit_Display hex_digit_display_1 (.value(ALU_o_p_3));  // open: dp
  Hex_Digit_Display hex_digit_display_2 (.value(ALU_o_p_4));  // open: dp
  Register #(.width(16)) RZ (
    .D({ALU_o_p_4, ALU_o_p_3, ALU_o_p_2, ALU_o_p}), .Q(RZ_q), .clk(Clock_out), .clr(in_2));  // open: en
  Hex_Digit_Display hex_digit_display_3 (.value(ALU_o_p_2));  // open: dp
  Hex_Digit_Display hex_digit_display_4 (.value(ALU_o_p));  // open: dp

  // Other names for the same wires on the sheet: RESET = in_2

  // Notes on the sheet:
  //   Code Memory
  //   contents of rom_1 (hex, n*v repeats v):
  //   25220 26554
  //   Data Memory
  //   ADD R5,R2,[0X20]
  //   OX20--->0X0C
  //   0X0C---->02
  //   0010 0101 0010 0010 0000
endmodule

module ALU__8_bit (
  input  [7:0] A,
  input  [7:0] B,
  input  [3:0] Opcode,
  output [15:0] O_p
);

  wire adder_1_cout, decrement_1_cout, increment_1_cout, subtractor_1_bout;
  wire [2:0] bit_extender_1_out;
  wire [7:0] adder_1_out, and_1_out, bit_extender_4_out, bit_extender_5_out, bit_extender_6_out,
       bit_extender_7_out, decrement_1_s0, divider_1_out, divider_1_rem, increment_1_s0, multiplier_1_cout,
       multiplier_1_out, not_1_out, or_1_out, shifter_2_out, shifter_3_out, shifter_4_out, shifter_5_out,
       subtractor_1_out, xor_1_out;
  wire [15:0] bit_extender_2_out, bit_extender_3_out, bit_extender_8_out, bit_extender_9_out,
       bit_extender_10_out, bit_extender_11_out, bit_extender_12_out, bit_extender_13_out,
       bit_extender_14_out, bit_extender_15_out, shifter_1_out;

  Hex_Digit_Display hex_digit_display_1 (.value(A[7:4]));  // open: dp
  Hex_Digit_Display hex_digit_display_2 (.value(A[3:0]));  // open: dp
  Hex_Digit_Display hex_digit_display_3 (.value(B[7:4]));  // open: dp
  Hex_Digit_Display hex_digit_display_4 (.value(B[3:0]));  // open: dp
  Bit_Extender #(.out_width(3)) bit_extender_1 (.in(B), .out(bit_extender_1_out));
  assign bit_extender_2_out = {{8{1'b0}}, B};  // Bit_Extender bit_extender_2
  Increment increment_1 (
    .A0(A[0]), .A1(A[1]), .A2(A[2]), .A3(A[3]), .A4(A[4]), .A5(A[5]), .A6(A[6]), .A7(A[7]), .B0(B[0]),
    .B1(B[1]), .B2(B[2]), .B3(B[3]), .B4(B[4]), .B5(B[5]), .B6(B[6]), .B7(B[7]), .S0(increment_1_s0[0]),
    .S1(increment_1_s0[1]), .S2(increment_1_s0[2]), .S3(increment_1_s0[3]), .S4(increment_1_s0[4]),
    .S5(increment_1_s0[5]), .S6(increment_1_s0[6]), .S7(increment_1_s0[7]), .Cout(increment_1_cout));  // open: C_in
  Decrement decrement_1 (
    .A0(A[0]), .A1(A[1]), .A2(A[2]), .A3(A[3]), .A4(A[4]), .A5(A[5]), .A6(A[6]), .A7(A[7]), .B0(B[0]),
    .B1(B[1]), .B2(B[2]), .B3(B[3]), .B4(B[4]), .B5(B[5]), .B6(B[6]), .B7(B[7]), .S0(decrement_1_s0[0]),
    .S1(decrement_1_s0[1]), .S2(decrement_1_s0[2]), .S3(decrement_1_s0[3]), .S4(decrement_1_s0[4]),
    .S5(decrement_1_s0[5]), .S6(decrement_1_s0[6]), .S7(decrement_1_s0[7]), .Cout(decrement_1_cout));  // open: C_in
  assign not_1_out = ~A;  // NOT_Gate not_1, 8 bits wide
  assign bit_extender_3_out = {{8{1'b0}}, A};  // Bit_Extender bit_extender_3
  Adder adder_1 (.a(A), .b(B), .out(adder_1_out), .cout(adder_1_cout));  // open: cin
  assign bit_extender_4_out = {{7{1'b0}}, adder_1_cout};  // Bit_Extender bit_extender_4
  Subtractor subtractor_1 (.a(A), .b(B), .out(subtractor_1_out), .bout(subtractor_1_bout));  // open: bin
  assign bit_extender_5_out = {{7{1'b0}}, subtractor_1_bout};  // Bit_Extender bit_extender_5
  Multiplier multiplier_1 (.a(A), .b(A), .out(multiplier_1_out), .cout(multiplier_1_cout));  // open: cin
  Divider divider_1 (.a(A), .b(A), .out(divider_1_out), .rem(divider_1_rem));  // open: upper
  assign and_1_out = A & B;  // AND_Gate and_1, 8 bits wide
  assign or_1_out = A | B;  // OR_Gate or_1, 8 bits wide
  assign xor_1_out = A ^ B;  // XOR_Gate xor_1, 8 bits wide
  assign bit_extender_6_out = {{7{1'b0}}, increment_1_cout};  // Bit_Extender bit_extender_6
  assign bit_extender_7_out = {{7{1'b0}}, decrement_1_cout};  // Bit_Extender bit_extender_7
  Shifter #(.width(16)) shifter_1 (.in(bit_extender_3_out), .\dist (4'b0000), .out(shifter_1_out));
  assign bit_extender_8_out = {{8{1'b0}}, and_1_out};  // Bit_Extender bit_extender_8
  assign bit_extender_9_out = {{8{1'b0}}, or_1_out};  // Bit_Extender bit_extender_9
  assign bit_extender_10_out = {{8{1'b0}}, not_1_out};  // Bit_Extender bit_extender_10
  Shifter #(.shift("lr")) shifter_2 (.in(A), .\dist (bit_extender_1_out), .out(shifter_2_out));
  Shifter shifter_3 (.in(A), .\dist (bit_extender_1_out), .out(shifter_3_out));
  Shifter #(.shift("rr")) shifter_4 (.in(A), .\dist (bit_extender_1_out), .out(shifter_4_out));
  Shifter #(.shift("rl")) shifter_5 (.in(A), .\dist (bit_extender_1_out), .out(shifter_5_out));
  assign bit_extender_11_out = {{8{1'b0}}, xor_1_out};  // Bit_Extender bit_extender_11
  assign bit_extender_12_out = {{8{1'b0}}, shifter_2_out};  // Bit_Extender bit_extender_12
  assign bit_extender_13_out = {{8{1'b0}}, shifter_3_out};  // Bit_Extender bit_extender_13
  assign bit_extender_14_out = {{8{1'b0}}, shifter_4_out};  // Bit_Extender bit_extender_14
  assign bit_extender_15_out = {{8{1'b0}}, shifter_5_out};  // Bit_Extender bit_extender_15
  Hex_Digit_Display hex_digit_display_5 (.value(O_p[15:12]));  // open: dp
  Multiplexer #(.select(4), .width(16), .enable("false")) multiplexer_1 (
    .in0(bit_extender_2_out), .in1(shifter_1_out), .in2({bit_extender_4_out, adder_1_out}),
    .in3({bit_extender_5_out, subtractor_1_out}), .in4({multiplier_1_cout, multiplier_1_out}),
    .in5({divider_1_rem, divider_1_out}), .in6({bit_extender_6_out, increment_1_s0}),
    .in7({bit_extender_7_out, decrement_1_s0}), .in8(bit_extender_8_out), .in9(bit_extender_9_out),
    .in10(bit_extender_10_out), .in11(bit_extender_11_out), .in12(bit_extender_12_out),
    .in13(bit_extender_13_out), .in14(bit_extender_14_out), .in15(bit_extender_15_out), .out(O_p),
    .sel(Opcode));
  Hex_Digit_Display hex_digit_display_6 (.value(O_p[11:8]));  // open: dp
  Hex_Digit_Display hex_digit_display_7 (.value(O_p[3:0]));  // open: dp
  Hex_Digit_Display hex_digit_display_8 (.value(O_p[7:4]));  // open: dp
endmodule

module Increment (
  input  C_in,
  input  A0,
  input  A1,
  input  A2,
  input  A3,
  input  A4,
  input  A5,
  input  A6,
  input  A7,
  input  B0,
  input  B1,
  input  B2,
  input  B3,
  input  B4,
  input  B5,
  input  B6,
  input  B7,
  output S0,
  output S1,
  output S2,
  output S3,
  output S4,
  output S5,
  output S6,
  output S7,
  output Cout
);

  wire adder_1_cout, adder_2_cout, adder_3_cout, adder_4_cout, adder_5_cout, adder_6_cout, adder_7_cout;

  Adder #(.width(1)) adder_1 (.a(A0), .b(B0), .out(S0), .cin(C_in), .cout(adder_1_cout));
  Adder #(.width(1)) adder_2 (.a(A1), .b(B1), .out(S1), .cin(adder_1_cout), .cout(adder_2_cout));
  Adder #(.width(1)) adder_3 (.a(A2), .b(B2), .out(S2), .cin(adder_2_cout), .cout(adder_3_cout));
  Adder #(.width(1)) adder_4 (.a(A3), .b(B3), .out(S3), .cin(adder_3_cout), .cout(adder_4_cout));
  Adder #(.width(1)) adder_5 (.a(A4), .b(B4), .out(S4), .cin(adder_4_cout), .cout(adder_5_cout));
  Adder #(.width(1)) adder_6 (.a(A5), .b(B5), .out(S5), .cin(adder_5_cout), .cout(adder_6_cout));
  Adder #(.width(1)) adder_7 (.a(A6), .b(B6), .out(S6), .cin(adder_6_cout), .cout(adder_7_cout));
  Adder #(.width(1)) adder_8 (.a(A7), .b(B7), .out(S7), .cin(adder_7_cout), .cout(Cout));
endmodule

module Decrement (
  input  C_in,
  input  A0,
  input  A1,
  input  A2,
  input  A3,
  input  A4,
  input  A5,
  input  A6,
  input  A7,
  input  B0,
  input  B1,
  input  B2,
  input  B3,
  input  B4,
  input  B5,
  input  B6,
  input  B7,
  output S0,
  output S1,
  output S2,
  output S3,
  output S4,
  output S5,
  output S6,
  output S7,
  output Cout
);

  wire subtractor_1_bout, subtractor_2_bout, subtractor_3_bout, subtractor_4_bout, subtractor_5_bout,
       subtractor_6_bout, subtractor_7_bout;

  Subtractor #(.width(1)) subtractor_1 (.a(A0), .b(B0), .out(S0), .bin(C_in), .bout(subtractor_1_bout));
  Subtractor #(.width(1)) subtractor_2 (.a(A1), .b(B1), .out(S1), .bin(subtractor_1_bout), .bout(subtractor_2_bout));
  Subtractor #(.width(1)) subtractor_3 (.a(A2), .b(B2), .out(S2), .bin(subtractor_2_bout), .bout(subtractor_3_bout));
  Subtractor #(.width(1)) subtractor_4 (.a(A3), .b(B3), .out(S3), .bin(subtractor_3_bout), .bout(subtractor_4_bout));
  Subtractor #(.width(1)) subtractor_5 (.a(A4), .b(B4), .out(S4), .bin(subtractor_4_bout), .bout(subtractor_5_bout));
  Subtractor #(.width(1)) subtractor_6 (.a(A5), .b(B5), .out(S5), .bin(subtractor_5_bout), .bout(subtractor_6_bout));
  Subtractor #(.width(1)) subtractor_7 (.a(A6), .b(B6), .out(S6), .bin(subtractor_6_bout), .bout(subtractor_7_bout));
  Subtractor #(.width(1)) subtractor_8 (.a(A7), .b(B7), .out(S7), .bin(subtractor_7_bout), .bout(Cout));
endmodule

// Register Bank
module Register_Bank (
  input  [7:0] Data_in,
  input  [3:0] Rx__4bit,
  input  Clock,
  input  R_W,
  output [7:0] Data_Out
);

  wire decoder_1_out0, decoder_1_out1, decoder_1_out2, decoder_1_out3, decoder_1_out4, decoder_1_out5,
       decoder_1_out6, decoder_1_out7, decoder_1_out8, decoder_1_out9, decoder_1_out10, decoder_1_out11,
       decoder_1_out12, decoder_1_out13, decoder_1_out14, decoder_1_out15, not_1_out, undriven, undriven_2,
       undriven_3, undriven_4, undriven_5, undriven_6, undriven_7, undriven_8, undriven_9, undriven_10,
       undriven_11, undriven_12, undriven_13, undriven_14, undriven_15;
  wire [7:0] R0_q, R1_q, R2_q, R3_q, R4_q, R5_q, R6_q, R7_q, R8_q, R9_q, R10_q, R11_q, R12_q, R13_q, R14_q,
       R15_q;

  not not_1 (not_1_out, R_W);
  Decoder #(.select(4), .disabled(0)) decoder_1 (
    .out0(decoder_1_out0), .out1(decoder_1_out1), .out2(decoder_1_out2), .out3(decoder_1_out3),
    .out4(decoder_1_out4), .out5(decoder_1_out5), .out6(decoder_1_out6), .out7(decoder_1_out7),
    .out8(decoder_1_out8), .out9(decoder_1_out9), .out10(decoder_1_out10), .out11(decoder_1_out11),
    .out12(decoder_1_out12), .out13(decoder_1_out13), .out14(decoder_1_out14), .out15(decoder_1_out15),
    .sel(Rx__4bit), .en(not_1_out));
  Register R0 (.D(Data_in), .en(decoder_1_out0), .Q(R0_q), .clk(Clock));  // open: clr
  Register R1 (.D(Data_in), .en(decoder_1_out1), .Q(R1_q), .clk(Clock), .clr(undriven));
  Register R2 (.D(Data_in), .en(decoder_1_out2), .Q(R2_q), .clk(Clock), .clr(undriven_2));
  Register R3 (.D(Data_in), .en(decoder_1_out3), .Q(R3_q), .clk(Clock), .clr(undriven_3));
  Register R4 (.D(Data_in), .en(decoder_1_out4), .Q(R4_q), .clk(Clock), .clr(undriven_4));
  Register R5 (.D(Data_in), .en(decoder_1_out5), .Q(R5_q), .clk(Clock), .clr(undriven_5));
  Register R6 (.D(Data_in), .en(decoder_1_out6), .Q(R6_q), .clk(Clock), .clr(undriven_6));
  Register R7 (.D(Data_in), .en(decoder_1_out7), .Q(R7_q), .clk(Clock), .clr(undriven_7));
  Register R8 (.D(Data_in), .en(decoder_1_out8), .Q(R8_q), .clk(Clock), .clr(undriven_8));
  Register R9 (.D(Data_in), .en(decoder_1_out9), .Q(R9_q), .clk(Clock), .clr(undriven_9));
  Register R10 (.D(Data_in), .en(decoder_1_out10), .Q(R10_q), .clk(Clock), .clr(undriven_10));
  Register R11 (.D(Data_in), .en(decoder_1_out11), .Q(R11_q), .clk(Clock), .clr(undriven_11));
  Register R12 (.D(Data_in), .en(decoder_1_out12), .Q(R12_q), .clk(Clock), .clr(undriven_12));
  Register R13 (.D(Data_in), .en(decoder_1_out13), .Q(R13_q), .clk(Clock), .clr(undriven_13));
  Register R14 (.D(Data_in), .en(decoder_1_out14), .Q(R14_q), .clk(Clock), .clr(undriven_14));
  Register R15 (.D(Data_in), .en(decoder_1_out15), .Q(R15_q), .clk(Clock), .clr(undriven_15));
  Multiplexer #(.select(4), .width(8)) multiplexer_1 (
    .in0(R0_q), .in1(R1_q), .in2(R2_q), .in3(R3_q), .in4(R4_q), .in5(R5_q), .in6(R6_q), .in7(R7_q),
    .in8(R8_q), .in9(R9_q), .in10(R10_q), .in11(R11_q), .in12(R12_q), .in13(R13_q), .in14(R14_q),
    .in15(R15_q), .out(Data_Out), .sel(Rx__4bit), .en(R_W));
endmodule

module PC (
  input  [7:0] PC_In,
  input  Clock,
  input  PC_Enable,
  input  Reset,
  output [7:0] PC_Out
);

  wire [7:0] adder_1_out;

  Adder adder_1 (.a(PC_In), .b(PC_Out), .out(adder_1_out), .cin(1'b1));  // open: cout
  Hex_Digit_Display hex_digit_display_1 (.value(PC_Out[7:4]));  // open: dp
  Register register_1 (.D(adder_1_out), .en(PC_Enable), .Q(PC_Out), .clk(Clock), .clr(Reset));
  Hex_Digit_Display hex_digit_display_2 (.value(PC_Out[3:0]));  // open: dp
endmodule
